// Logisim project main.circ as structural Verilog: 5 circuits, main circuit main
module main (
);

  wire and_1_out, and_2_out, and_3_out, clock_1_out, control_1_is_imm, control_1_jmp, control_1_jnz,
       control_1_jz, control_1_lastcycle, control_1_st, control_1_we, is_not_zero_1_out_2, not_1_out,
       not_2_out, or_1_out, register_2_q;
  wire [1:0] control_1_src;
  wire [2:0] control_1_op, control_1_r0, control_1_r1;
  wire [7:0] control_1_imm8;
  wire [15:0] adder_1_out, alu_1_out, controlled_buffer_1_out, controlled_buffer_3_out, IP_q,
       multiplexer_1_out, multiplexer_2_out, multiplexer_3_out, ram_1_data, reg_file_1_r0d, reg_file_1_r1d,
       register_1_q;

  Clock clock_1 (.out(clock_1_out));
  Reg_File reg_file_1 (
    .R0d(reg_file_1_r0d), .R1d(reg_file_1_r1d), .CLK(clock_1_out), .in(multiplexer_1_out), .R0(control_1_r0),
    .R1(control_1_r1), .WE(control_1_we));
  Multiplexer #(.select(2), .width(16), .disabled(0), .enable("false")) multiplexer_1 (
    .in0(multiplexer_3_out), .in1(alu_1_out), .in2(ram_1_data), .out(multiplexer_1_out), .sel(control_1_src));  // open: in3
  Adder #(.width(16)) adder_1 (.a(IP_q), .b({16{1'b0}}), .out(adder_1_out), .cin(control_1_lastcycle));  // open: cout
  or or_1 (or_1_out, and_3_out, and_2_out, and_1_out);
  and and_1 (and_1_out, control_1_jmp, 1'b1);
  and and_2 (and_2_out, control_1_jnz, is_not_zero_1_out_2);
  and and_3 (and_3_out, control_1_jz, ~is_not_zero_1_out_2);  // AND_Gate
  Multiplexer #(.width(16), .disabled(0), .enable("false")) multiplexer_2 (
    .in0(adder_1_out), .in1(multiplexer_3_out), .out(multiplexer_2_out), .sel(or_1_out));
  Register #(.width(16)) IP (.D(multiplexer_2_out), .en(1'b1), .Q(IP_q), .clk(clock_1_out));  // open: clr
  is_not_zero is_not_zero_1 (.in_1(reg_file_1_r0d), .out_2(is_not_zero_1_out_2));
  Multiplexer #(.width(16), .disabled(0), .enable("false")) multiplexer_3 (
    .in0(reg_file_1_r1d), .in1({{8{1'b0}}, control_1_imm8}), .out(multiplexer_3_out), .sel(control_1_is_imm));
  assign controlled_buffer_1_out = control_1_lastcycle ? IP_q : 16'bz;  // Controlled_Buffer controlled_buffer_1
  not not_1 (not_1_out, control_1_lastcycle);
  assign controlled_buffer_1_out = not_1_out ? multiplexer_3_out : 16'bz;  // Controlled_Buffer controlled_buffer_2
  Control control_1 (
    .INSTR(register_1_q), .R0(control_1_r0), .R1(control_1_r1), .is_imm(control_1_is_imm),
    .imm8(control_1_imm8), .OP(control_1_op), .JMP(control_1_jmp), .JNZ(control_1_jnz), .JZ(control_1_jz),
    .ST(control_1_st), .WE(control_1_we), .SRC(control_1_src), .lastcycle(control_1_lastcycle),
    .next(register_2_q), .CLK(clock_1_out));  // open: WRW
  assign controlled_buffer_3_out = control_1_lastcycle ? ram_1_data : 16'bz;  // Controlled_Buffer controlled_buffer_3
  Register #(.width(16)) register_1 (
    .D(controlled_buffer_3_out), .en(control_1_lastcycle), .Q(register_1_q), .clk(clock_1_out));  // open: clr
  not not_2 (not_2_out, control_1_lastcycle);
  Register #(.width(1)) register_2 (.D(not_2_out), .Q(register_2_q), .clk(clock_1_out));  // open: en, clr
  ALU alu_1 (.IN0(reg_file_1_r0d), .IN1(multiplexer_3_out), .OUT(alu_1_out), .OP(control_1_op));
  RAM #(.addrWidth(16), .dataWidth(16), .bus("separate")) ram_1 (
    .addr(controlled_buffer_1_out), .din(reg_file_1_r0d), .data(ram_1_data), .str(control_1_st),
    .clk(clock_1_out), .ld(1'b1));  // open: sel, clr

  // Notes on the sheet:
  //   OPERANDS WE  SRC imm8   is_imm    R0 R1    STR    OP  INSTR MEM  ALU   ADDR
endmodule

module ALU (
  input  [2:0] OP,
  input  [15:0] IN0,
  input  [15:0] IN1,
  output [15:0] OUT
);

  wire [15:0] adder_1_out, and_1_out, not_1_out, or_1_out, shifter_1_out, shifter_2_out, subtractor_1_out,
       xor_1_out;

  Adder #(.width(16)) adder_1 (.a(IN0), .b(IN1), .out(adder_1_out));  // open: cin, cout
  Subtractor #(.width(16)) subtractor_1 (.a(IN0), .b(IN1), .out(subtractor_1_out));  // open: bin, bout
  assign not_1_out = ~IN1;  // NOT_Gate not_1, 16 bits wide
  assign and_1_out = IN0 & IN1;  // AND_Gate and_1, 16 bits wide
  assign or_1_out = IN0 | IN1;  // OR_Gate or_1, 16 bits wide
  assign xor_1_out = IN0 ^ IN1;  // XOR_Gate xor_1, 16 bits wide
  Shifter #(.width(16)) shifter_1 (.in(IN0), .\dist (IN1[3:0]), .out(shifter_1_out));
  Shifter #(.width(16), .shift("lr")) shifter_2 (.in(IN0), .\dist (IN1[3:0]), .out(shifter_2_out));
  Multiplexer #(.select(3), .width(16), .disabled(0), .enable("false")) multiplexer_1 (
    .in0(adder_1_out), .in1(subtractor_1_out), .in2(not_1_out), .in3(and_1_out), .in4(or_1_out),
    .in5(xor_1_out), .in6(shifter_1_out), .in7(shifter_2_out), .out(OUT), .sel(OP));
endmodule

module Reg_File (
  input  CLK,
  input  [2:0] R0,
  input  [2:0] R1,
  input  WE,
  input  [15:0] in,
  output [15:0] R0d,
  output [15:0] R1d
);

  wire demultiplexer_1_out0, demultiplexer_1_out1, demultiplexer_1_out2, demultiplexer_1_out3,
       demultiplexer_1_out4, demultiplexer_1_out5, demultiplexer_1_out6, demultiplexer_1_out7;
  wire [15:0] register_1_q, register_2_q, register_3_q, register_4_q, register_5_q, register_6_q,
       register_7_q, register_8_q;

  Demultiplexer #(.select(3), .disabled(0), .enable("false")) demultiplexer_1 (
    .out0(demultiplexer_1_out0), .out1(demultiplexer_1_out1), .out2(demultiplexer_1_out2),
    .out3(demultiplexer_1_out3), .out4(demultiplexer_1_out4), .out5(demultiplexer_1_out5),
    .out6(demultiplexer_1_out6), .out7(demultiplexer_1_out7), .in(WE), .sel(R0));
  Register #(.width(16)) register_1 (.D(in), .en(demultiplexer_1_out0), .Q(register_1_q), .clk(CLK));  // open: clr
  Register #(.width(16)) register_2 (.D(in), .en(demultiplexer_1_out1), .Q(register_2_q), .clk(CLK));  // open: clr
  Register #(.width(16)) register_3 (.D(in), .en(demultiplexer_1_out2), .Q(register_3_q), .clk(CLK));  // open: clr
  Register #(.width(16)) register_4 (.D(in), .en(demultiplexer_1_out3), .Q(register_4_q), .clk(CLK));  // open: clr
  Register #(.width(16)) register_5 (.D(in), .en(demultiplexer_1_out4), .Q(register_5_q), .clk(CLK));  // open: clr
  Register #(.width(16)) register_6 (.D(in), .en(demultiplexer_1_out5), .Q(register_6_q), .clk(CLK));  // open: clr
  Register #(.width(16)) register_7 (.D(in), .en(demultiplexer_1_out6), .Q(register_7_q), .clk(CLK));  // open: clr
  Register #(.width(16)) register_8 (.D(in), .en(demultiplexer_1_out7), .Q(register_8_q), .clk(CLK));  // open: clr
  Multiplexer #(.select(3), .width(16), .disabled(0), .enable("false")) multiplexer_1 (
    .in0(register_1_q), .in1(register_2_q), .in2(register_3_q), .in3(register_4_q), .in4(register_5_q),
    .in5(register_6_q), .in6(register_7_q), .in7(register_8_q), .out(R0d), .sel(R0));
  Multiplexer #(.select(3), .width(16), .disabled(0), .enable("false")) multiplexer_2 (
    .in0(register_1_q), .in1(register_2_q), .in2(register_3_q), .in3(register_4_q), .in4(register_5_q),
    .in5(register_6_q), .in6(register_7_q), .in7(register_8_q), .out(R1d), .sel(R1));
endmodule

module Control (
  input  next,
  input  CLK,
  input  [15:0] INSTR,
  output [2:0] R0,
  output [2:0] R1,
  output is_imm,
  output [7:0] imm8,
  output [2:0] OP,
  output lastcycle,
  output [1:0] SRC,
  output WE,
  output ST,
  output WRW,
  output JMP,
  output JNZ,
  output JZ
);

  wire adder_1_out, not_1_out, register_1_q;
  wire [8:0] rom_1_data;

  ROM #(.addrWidth(4), .dataWidth(9)) rom_1 (.addr(INSTR[15:12]), .data(rom_1_data));  // open: sel
  Adder #(.width(1)) adder_1 (.a(register_1_q), .b(1'b1), .out(adder_1_out));  // open: cin, cout
  Multiplexer #(.width(9), .disabled(0), .enable("false")) multiplexer_1 (
    .in0(rom_1_data), .in1(9'h100), .out({lastcycle, SRC, WE, ST, WRW, JMP, JNZ, JZ}), .sel(register_1_q));
  Register #(.width(1)) register_1 (.D(adder_1_out), .en(1'b1), .Q(register_1_q), .clk(CLK), .clr(not_1_out));
  not not_1 (not_1_out, next);

  assign imm8 = INSTR[7:0];
  assign is_imm = INSTR[8];
  assign OP = INSTR[14:12];
  assign R0 = INSTR[11:9];
  assign R1 = INSTR[2:0];

  // Notes on the sheet:
  //   contents of rom_1 (hex, n*v repeats v):
  //   120 a0 10 1e0 108 104 102 101 8*160
endmodule

module is_not_zero (
  input  [15:0] in_1,
  output out_2
);

  or or_1 (out_2, in_1[0], in_1[1], in_1[2], in_1[3], in_1[4], in_1[5], in_1[6], in_1[7], in_1[8], in_1[9], in_1[10], in_1[11], in_1[12], in_1[13], in_1[14], in_1[15]);
endmodule
